# Fritzing sketch Schaltungsaufbau (saved by Fritzing 0.9.1b)
breadboards: 1

parts:
  Bauteil4 = Arduino Pro Mini v13
  U1 = RF-LINK_TX [package=rf-link_tx]
  R1 = Photocell (LDR) [package=THT]
  R2 = Resistor [tolerance=±5% resistance=22k package=THT]

nets:
  GND: Bauteil4.GND, U1.GND, R2.Pin_1
  N1: Bauteil4.A3, U1.+5V
  N2: Bauteil4.A2, R1.pin_1
  N3: Bauteil4.A1, R1.pin_0, R2.Pin_0
  N4: Bauteil4.D13/SCK, U1.DATA
