# Fritzing sketch Bild_2.12_Arduino+Raspberry_Pi_I2C-Verbindung (saved by Fritzing 0.8.7b)

parts:
  Raspberry_Pi_B_rev1 = Raspberry Pi B rev2
  Bauteil1 = Arduino Uno (Rev3)

nets:
  N1: Raspberry_Pi_B_rev1.GPIO_2, Raspberry_Pi_B_rev1.5V, Bauteil1.A4/SDA
  N2: Raspberry_Pi_B_rev1.GPIO_3, Bauteil1.A5/SCL
  GND: Raspberry_Pi_B_rev1.GND, Bauteil1.GND
