# Fritzing sketch Bild_2.19_Pro_Mini_Bootloader_flashen (saved by Fritzing 0.8.7b)
circuit board: 16.9333cm x 5.64444cm

parts:
  C1_10µF = Electrolytic Capacitor [capacitance=1µF package="100 mil [THT, electrolytic]"]
  Bauteil1 = Arduino Uno (Rev3)
  Bauteil2 = Arduino Pro Mini v13

nets:
  GND: C1_10µF.-, Bauteil1.GND, Bauteil2.GND
  N1: C1_10µF.+, Bauteil1.RESET
  N2: Bauteil1.D10_PWM/SS, Bauteil2.RESET
  N3: Bauteil1.D11_PWM/MOSI, Bauteil2.D11_PWM/MOSI
  N4: Bauteil1.D12/MISO, Bauteil2.D12/MISO
  N5: Bauteil1.D13/SCK, Bauteil2.D13/SCK
  N6: Bauteil1.5V, Bauteil2.RAW
