# Fritzing sketch Bild_2.23_Arduino_als_ISP_flasht_Bootloader_auf_Atmega328 (saved by Fritzing 0.8.7b)
circuit board: 8.46667cm x 5.64444cm
breadboards: 1

parts:
  Bauteil2 = Arduino Uno (Rev3)
  U2 = atmega328 [package=dip]
  XTAL2 = Crystal [frequency="16 Mhz" package=THT]
  C2 = Capacitor [package=cap-pth-small2]
  C3 = Capacitor [package=cap-pth-small2]
  C4 = Electrolytic Capacitor [capacitance=100µF package="200 mil [THT, electrolytic]"]

nets:
  N1: Bauteil2.D10_PWM/SS, U2.RESET
  N2: Bauteil2.D11_PWM/MOSI, U2.D11_(PWM)
  N3: Bauteil2.D12/MISO, U2.D12
  N4: Bauteil2.D13/SCK, U2.D13
  GND: Bauteil2.GND, U2.GND, C2.2, C3.1, C4.+
  N5: Bauteil2.RESET, C4.-
  5V: Bauteil2.5V, U2.VCC, U2.AVCC
  N6: U2.XLAT1, U2.XLAT2, XTAL2.pin_0, XTAL2.pin_1, C2.1, C3.2
