# Fritzing sketch Bild_2.24_mit_FTDI_(Errata)_Widerstand_korrigiert (saved by Fritzing 0.8.7b)
circuit board: 8.46667cm x 5.64444cm
breadboards: 1

parts:
  Bauteil1 = FTDI Basic Programmer
  U1 = atmega328 [package=dip]
  LED1 = LED - 5mm [color="Red (633nm)" package="5 mm [THT]"]
  R1 = Resistor [tolerance=±5% resistance=220 package=THT]
  C1 = Capacitor [package=cap-pth-small-kit]
  R2 = Resistor [tolerance=±5% resistance=10k package=THT]

nets (from the pcb view):
  N1: Bauteil1.DTR, C1.1
  N2: Bauteil1.RXI, U1.D1_(TX)
  N3: Bauteil1.TXO, U1.D0_(RX)
  N4: Bauteil1.POWER, U1.VCC, U1.AVCC
  GND: Bauteil1.GND, U1.GND, R1.Pin_1, R2.Pin_0
  N5: U1.RESET, C1.2, R2.Pin_1
  N6: U1.D13, LED1.anode
  N7: LED1.cathode, R1.Pin_0
