# Fritzing sketch Bild_2.26_ohne_Kondensator_(Errata)_Widerstand_korrigiert (saved by Fritzing 0.8.7b)
circuit board: 8.46667cm x 5.64444cm
breadboards: 1

parts:
  Bauteil1 = FTDI Basic Programmer
  U1 = atmega328 [package=dip]
  LED1 = LED - 5mm [color="Red (633nm)" package="5 mm [THT]"]
  R1 = Resistor [tolerance=±5% resistance=220 package=THT]
  R2 = Resistor [tolerance=±5% resistance=10k package=THT]

nets:
  N1: Bauteil1.POWER, U1.VCC, U1.AVCC, R2.Pin_0
  GND: Bauteil1.GND, U1.GND, R1.Pin_1
  N2: U1.RESET, R2.Pin_1
  N3: U1.D13, LED1.anode
  N4: LED1.cathode, R1.Pin_0
