# Fritzing sketch Bild_2.29_Attiny45_mit_Uno_als_ISP (saved by Fritzing 0.8.7b)
breadboards: 1

parts:
  Bauteil2 = Arduino Uno (Rev3)
  C4 = Electrolytic Capacitor [capacitance=100µF package="200 mil [THT, electrolytic]"]
  U3 = ATTINY45 [package=dip]

nets:
  N1: Bauteil2.D10_PWM/SS, U3.PB5(NRES)
  N2: Bauteil2.D11_PWM/MOSI, U3.PB0(MOSI)
  N3: Bauteil2.D12/MISO, U3.PB1(MISO)
  N4: Bauteil2.D13/SCK, U3.PB2(SCK_ADC1)
  GND: Bauteil2.GND, C4.+, U3.GND
  N5: Bauteil2.RESET, C4.-
  5V: Bauteil2.5V, U3.VCC
