# Fritzing sketch Bild_3.02_RF-Link-Sender_an_Uno (saved by Fritzing 0.8.7b)

parts:
  U1 = RF-LINK_TX [package=rf-link_tx]
  Bauteil1 = Arduino Uno (Rev3)

nets:
  N1: U1.DATA, Bauteil1.D10_PWM/SS
  GND: U1.GND, Bauteil1.GND
  +5V: U1.+5V, Bauteil1.5V
