# Fritzing sketch Bild_3.04_DS3231_RTC_an_Uno (saved by Fritzing 0.8.7b)

parts:
  Bauteil1 = Arduino Uno (Rev3)
  Bauteil2 = Real Time Clock Module - DS1307 RTC Breakout Board

nets:
  N1: Bauteil1.A4/SDA, Bauteil2.SDA
  N2: Bauteil1.A5/SCL, Bauteil2.SCL
  5V: Bauteil1.5V, Bauteil2.5V
  GND: Bauteil1.GND, Bauteil2.GND
