# Fritzing sketch Bild_3.05_Funksteckdosenschaltuhr_RF-Link_mit_RTC (saved by Fritzing 0.8.7b)
breadboards: 1

parts:
  Bauteil1 = Arduino Uno (Rev3)
  Bauteil2 = Real Time Clock Module - DS1307 RTC Breakout Board
  U1 = RF-LINK_TX [package=rf-link_tx]

nets:
  N1: Bauteil1.A4/SDA, Bauteil2.SDA
  N2: Bauteil1.A5/SCL, Bauteil2.SCL
  N3: Bauteil1.D10_PWM/SS, U1.DATA
  GND: Bauteil1.GND, Bauteil2.GND, U1.GND
  5V: Bauteil1.5V, Bauteil2.5V, U1.+5V
