# Fritzing sketch Bild_3.07_Anschluss_DCF77 (saved by Fritzing 0.8.7b)
breadboards: 1

parts:
  Bauteil1 = Arduino Uno (Rev3)
  DCF77_Receiver_-_Conrad_1 = DCF77 641138
  R1 = Resistor [tolerance=±5% resistance=10k package=THT]

nets:
  N1: Bauteil1.GND, DCF77_Receiver_-_Conrad_1.Ground
  N2: Bauteil1.D2, DCF77_Receiver_-_Conrad_1.DCF_output, R1.Pin_0
  5V: Bauteil1.5V, DCF77_Receiver_-_Conrad_1.+5V, R1.Pin_1

custom parts:
  DCF77 641138: Low cost DCF77 receiver module. This is a radio receiver used in a radio clock, a quartz clock which is periodically set to the correct time by radio signals synchronized with an atomic clock from a government radio station. This one receives the coded time signals broadcast by German government time radio station DCF77 on 77.5 kHz. The ferrite loopstick (left) is the radio's antenna, and with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
