# Fritzing sketch Bild_3.08x_Anschluss_DCF77_und_RTC (saved by Fritzing 0.8.7b)
breadboards: 1

parts:
  Bauteil1 = Arduino Uno (Rev3)
  Bauteil2 = Real Time Clock Module - DS1307 RTC Breakout Board
  DCF77_Receiver_-_Conrad_1 = DCF77 641138

nets:
  N1: Bauteil1.A4/SDA, Bauteil2.SDA
  N2: Bauteil1.A5/SCL, Bauteil2.SCL
  GND: Bauteil1.GND, Bauteil2.GND, DCF77_Receiver_-_Conrad_1.Ground
  N3: Bauteil1.D2, DCF77_Receiver_-_Conrad_1.DCF_output
  5V: Bauteil1.5V, Bauteil2.5V, DCF77_Receiver_-_Conrad_1.+5V

custom parts:
  DCF77 641138: Low cost DCF77 receiver module. This is a radio receiver used in a radio clock, a quartz clock which is periodically set to the correct time by radio signals synchronized with an atomic clock from a government radio station. This one receives the coded time signals broadcast by German government time radio station DCF77 on 77.5 kHz. The ferrite loopstick (left) is the radio's antenna, and with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
