# Fritzing sketch Bild_3.18_Anschluss_RFM12B_an_5V_Arduino (saved by Fritzing 0.8.7b)
circuit board: 8.46667cm x 5.64444cm
breadboards: 1

parts:
  RFM12b1 = RFM12b HopeRF Transceiver
  R2 = Resistor [tolerance=±5% resistance=10k package=THT]
  R3 = Resistor [tolerance=±5% resistance=10k package=THT]
  R4 = Resistor [tolerance=±5% resistance=10k package=THT]
  R5 = Resistor [tolerance=±5% resistance=10k package=THT]
  R6 = Resistor [tolerance=±5% resistance=10k package=THT]
  Bauteil1 = Arduino Uno (Rev3)
  R7 = Resistor [tolerance=±5% resistance=10k package=THT]

nets:
  N1: RFM12b1.1_SDO, Bauteil1.D12/MISO
  N2: RFM12b1.6_nRES, Bauteil1.D2
  N3: RFM12b1.9_VDD, Bauteil1.3V3
  N4: RFM12b1.10_GND, R2.Pin_1, R3.Pin_1, Bauteil1.GND, R7.Pin_1
  N5: RFM12b1.12_SDI, R4.Pin_0, R7.Pin_0
  N6: RFM12b1.13_SCK, R2.Pin_0, R5.Pin_0
  N7: RFM12b1.14_nSEL, R3.Pin_0, R6.Pin_0
  N8: R4.Pin_1, Bauteil1.D11_PWM/MOSI
  N9: R5.Pin_1, Bauteil1.D13/SCK
  N10: R6.Pin_1, Bauteil1.D10_PWM/SS

notes:
  Antenne ca. 17cm für 433MHz
