# Fritzing sketch Bild_3.24_Anschluss_der_Transistoren_an_Thermostat (saved by Fritzing 0.8.7b)
breadboards: 1

parts:
  U1 = atmega328 [package=dip]
  Q1 = NPN-Transistor [package="TO92 [THT]"]
  Q2 = NPN-Transistor [package="TO92 [THT]"]
  R1 = Resistor [tolerance=±5% resistance=10k package=THT]
  R2 = Resistor [tolerance=±5% resistance=10k package=THT]

nets:
  N1: U1.VCC, U1.AVCC
  N2: U1.GND, Q1.E, Q2.E
  N3: U1.D11_(PWM), R2.Pin_0
  N4: U1.D12, R1.Pin_0
  N5: Q1.B, R2.Pin_1
  N6: Q2.B, R1.Pin_1

notes:
  < zum Batteriefach
  < zu den Knöpfen
  (links = hoch)
