# Fritzing sketch Bild_3.26_Thermostat_komplett_mit_Breadboard (saved by Fritzing 0.8.7b)
circuit board: 4.4306cm x 3.34489cm
breadboards: 1

parts:
  U1 = atmega328 [package=dip]
  Q1 = NPN-Transistor [package="TO92 [THT]"]
  Q2 = NPN-Transistor [package="TO92 [THT]"]
  R1 = Resistor [tolerance=±5% resistance=10k package=THT]
  R2 = Resistor [tolerance=±5% resistance=10k package=THT]
  RFM12b1 = RFM12b HopeRF Transceiver
  LED1 = LED - 5mm [color="Green (565nm)" package="5 mm [THT]"]
  R3 = Resistor [tolerance=±5% resistance=560 package=THT]

nets:
  N1: U1.D2, RFM12b1.6_nRES
  N2: U1.VCC, U1.AVCC
  N3: U1.GND, Q1.E, Q2.E, RFM12b1.9_VDD, RFM12b1.10_GND, R3.Pin_0
  N4: U1.D7, R1.Pin_0
  N5: U1.D8, R2.Pin_0
  N6: U1.D9_(PWM), LED1.cathode
  N7: U1.D10_(PWM), RFM12b1.14_nSEL
  N8: U1.D11_(PWM), RFM12b1.12_SDI
  N9: U1.D12, RFM12b1.1_SDO
  N10: U1.D13, RFM12b1.13_SCK
  N11: Q1.B, R2.Pin_1
  N12: Q2.B, R1.Pin_1
  N13: LED1.anode, R3.Pin_1

notes:
  < zum Batteriefach 3V
  < zu den Knöpfen
  (links = hoch)
