# Fritzing sketch Bild_3.29_Enc28J60_Anschluss (saved by Fritzing 0.8.7b)
circuit board: 8.46667cm x 5.64444cm
breadboards: 1

parts:
  R2 = Resistor [tolerance=±5% resistance=10k package=THT]
  R3 = Resistor [tolerance=±5% resistance=10k package=THT]
  R4 = Resistor [tolerance=±5% resistance=10k package=THT]
  R5 = Resistor [tolerance=±5% resistance=10k package=THT]
  R6 = Resistor [tolerance=±5% resistance=10k package=THT]
  Bauteil1 = Arduino Uno (Rev3)
  R7 = Resistor [tolerance=±5% resistance=10k package=THT]
  U1 = ENC28J60 [package=ssop28db]

nets:
  N1: R2.Pin_0, R5.Pin_0, U1.SCK
  N2: R2.Pin_1, R3.Pin_1, Bauteil1.GND, R7.Pin_1
  N3: R3.Pin_0, R6.Pin_0, U1.CS
  N4: R4.Pin_0, R7.Pin_0, U1.SI
  N5: R4.Pin_1, Bauteil1.D11_PWM/MOSI
  N6: R5.Pin_1, Bauteil1.D13/SCK
  N7: R6.Pin_1, Bauteil1.D10_PWM/SS
  N8: Bauteil1.D12/MISO, U1.SO
  N9: Bauteil1.D2, U1._INT
  N10: Bauteil1.RESET, U1.RESET
  3V3: Bauteil1.3V3, U1.VDD
