# Fritzing sketch Bild_3.33_RF-Link-Sender (saved by Fritzing 0.8.7b)

parts:
  Bauteil1 = Arduino Uno (Rev3)
  U1 = RF-LINK_TX [package=rf-link_tx]

nets:
  N1: Bauteil1.D12/MISO, U1.DATA
  N2: Bauteil1.D13/SCK, U1.+5V
  GND: Bauteil1.GND, U1.GND
