# Fritzing sketch Bild_3.38_Anschluss_Photowiderstand (saved by Fritzing 0.8.7b)
breadboards: 1

parts:
  Bauteil1 = Arduino Uno (Rev3)
  R1 = PHOTOCELL [package=photocell-kit]
  R2 = Resistor [tolerance=±5% resistance=22k package=THT]

nets:
  N1: Bauteil1.A0, R1.P$2, R2.Pin_0
  N2: Bauteil1.D13/SCK, R1.P$1
  N3: Bauteil1.GND, R2.Pin_1
