# Fritzing sketch Bild_3.41_Atmega328_als_Steuerungszentrale (saved by Fritzing 0.8.7b)
circuit board: 8.46667cm x 5.64444cm
breadboards: 1

parts:
  RFM12b1 = RFM12b HopeRF Transceiver
  R2 = Resistor [tolerance=±5% resistance=10k package=THT]
  R3 = Resistor [tolerance=±5% resistance=10k package=THT]
  R4 = Resistor [tolerance=±5% resistance=10k package=THT]
  R5 = Resistor [tolerance=±5% resistance=10k package=THT]
  R6 = Resistor [tolerance=±5% resistance=10k package=THT]
  Bauteil1 = Arduino Uno (Rev3)
  R7 = Resistor [tolerance=±5% resistance=10k package=THT]
  U1 = RF-LINK_TX [package=rf-link_tx]
  U2 = RF-LINK_RX [package=rf-link_rx]

nets:
  N1: RFM12b1.1_SDO, Bauteil1.D12/MISO
  N2: RFM12b1.6_nRES, Bauteil1.D2
  N3: RFM12b1.9_VDD, Bauteil1.3V3
  GND: RFM12b1.10_GND, R2.Pin_1, R3.Pin_1, R7.Pin_1, U1.GND, U2.GND
  N4: RFM12b1.12_SDI, R4.Pin_0, R7.Pin_0
  N5: RFM12b1.13_SCK, R2.Pin_0, R5.Pin_0
  N6: RFM12b1.14_nSEL, R3.Pin_0, R6.Pin_0
  N7: R4.Pin_1, Bauteil1.D11_PWM/MOSI
  N8: R5.Pin_1, Bauteil1.D13/SCK
  N9: R6.Pin_1, Bauteil1.D10_PWM/SS
  N10: Bauteil1.D3_PWM, U1.DATA
  N11: Bauteil1.D7, U2.DATA
  5V: Bauteil1.5V, U1.ANT, U2.+5V

notes:
  3x Antenne ca. 17cm für 433MHz
