# Fritzing sketch Bild_3.43_RFM12B_Yun_und_Leonardo (saved by Fritzing 0.8.7b)
circuit board: 8.46667cm x 5.64444cm
breadboards: 1

parts:
  RFM12b1 = RFM12b HopeRF Transceiver
  R2 = Resistor [tolerance=±5% resistance=10k package=THT]
  R3 = Resistor [tolerance=±5% resistance=10k package=THT]
  R4 = Resistor [tolerance=±5% resistance=10k package=THT]
  R5 = Resistor [tolerance=±5% resistance=10k package=THT]
  R6 = Resistor [tolerance=±5% resistance=10k package=THT]
  R7 = Resistor [tolerance=±5% resistance=10k package=THT]
  Bauteil2 = Arduino Leonardo (Rev3b)

nets:
  N1: RFM12b1.6_nRES, Bauteil2.D3_PWM/SCL
  N2: RFM12b1.9_VDD, Bauteil2.3V3
  N3: RFM12b1.10_GND, R2.Pin_1, R3.Pin_1, R7.Pin_1, Bauteil2.GND
  N4: RFM12b1.12_SDI, R4.Pin_0, R7.Pin_0
  N5: RFM12b1.13_SCK, R2.Pin_0, R5.Pin_0
  N6: RFM12b1.14_nSEL, R3.Pin_0, R6.Pin_0
  N7: R6.Pin_1, Bauteil2.D10_PWM/A10

notes:
  Antenne ca. 17cm für 433MHz
