# Fritzing sketch Bild_3.69_Taster_Interrupt (saved by Fritzing 0.8.7b)
breadboards: 1

parts:
  Bauteil1 = Arduino Uno (Rev3)
  S1 = Pushbutton [package="[THT]"]
  R1 = Resistor [tolerance=±5% resistance=1M package=THT]

nets:
  N1: Bauteil1.GND, R1.Pin_0
  N2: Bauteil1.D2, S1.Pin_1, S1.Pin_2
  N3: S1.Pin_3, S1.Pin_4, R1.Pin_1
