# Fritzing sketch Bild_3.79_Anschlussskizze_Waehlscheibe (saved by Fritzing 0.8.7b)
breadboards: 1

parts:
  Bauteil1 = Arduino Uno (Rev3)
  S1 = Pushbutton [package="[THT]"]
  R1 = Resistor [tolerance=±5% resistance=10k package=THT]
  LED1 = LED - 5mm [color="Red (633nm)" package="5 mm [THT]"]
  R2 = Resistor [tolerance=±5% resistance=1k package=THT]
  R3 = Resistor [tolerance=±5% resistance=1k package=THT]
  LED2 = LED - 5mm [color="Green (560nm)" package="5 mm [THT]"]

nets:
  N1: Bauteil1.D10_PWM/SS, R2.Pin_0
  N2: Bauteil1.D11_PWM/MOSI, R3.Pin_0
  N3: Bauteil1.D12/MISO, S1.Pin_3, S1.Pin_4, R1.Pin_1
  N4: Bauteil1.GND, R1.Pin_0, LED1.cathode, LED2.cathode
  N5: Bauteil1.5V, S1.Pin_1, S1.Pin_2
  N6: LED1.anode, R2.Pin_1
  N7: R3.Pin_1, LED2.anode
